# Fritzing sketch tempescope_remote_quick (saved by Fritzing 0.7.10b)
breadboards: 1

parts:
  Arduino1 = Arduino
  TX = IC, DIP package, 4 pins [chip_label=TX part_number=RF315-9912]

nets:
  N1: Arduino1.D12, TX.pin4
  N2: Arduino1.+5V, TX.pin3
  N3: Arduino1.GND, TX.pin1
